# Fritzing sketch KVM-Fritzing (saved by Fritzing 0.9.2b)
circuit board: 4.97342cm x 4.61531cm
breadboards: 1

parts:
  J1 = female pin header, 2 pins [form="♀ (female)"]
  J2 = female pin header, 2 pins [form="♀ (female)"]
  J3 = female pin header, 2 pins [form="♀ (female)"]
  LED1 = LED - 3mm [color="Red (633nm)" package="3 mm [THT]"]
  X5 = USB Connectors [package=usb-b-pth]
  X6 = USB Connectors [package=usb-a-h]
  X4 = USB Connectors [package=usb-b-pth]
  X2 = USB Connectors [package=usb-a-h]

nets:
  N1: J1.pin1, X6.D+, X2.D+
  N2: J1.pin2, X6.D-, X2.D-
  N3: J2.pin1, X5.D-
  N4: J2.pin2, X5.D+
  N5: J3.pin1, X4.D+
  N6: J3.pin2, X4.D-
  N7: LED1.cathode, X6.VBUS, X4.VBUS
  GND: LED1.anode, X6.GND, X4.GND
  GND_2: X5.GND, X2.GND
  N8: X5.VBUS, X2.VBUS

notes:
  openKVM
